// Logisim project hw4.circ as structural Verilog: 24 circuits, main circuit main
// PC Out
module main (
  input  reset,
  input  ResetMem
);

  wire alu_1_output_branch, ALUinB, beqz_1_beqz__rs, BR, branch_out, Clock, DMwe, JAL, JP, JR, KBenable,
       not_1_out, or_1_out, Rdst, Rwd, Rwe, TTYenable;
  wire [2:0] multiplexer_1_out, multiplexer_2_out, r7_1_r7, Rd, Rs, Rt, shamt;
  wire [3:0] ALUop, opcode, Top_4_PC_bits_top_4_pc_bits;
  wire [5:0] Immediate;
  wire [6:0] _7_bit__rs__7_bit__rs, keyboard_1_data;
  wire [11:0] Address;
  wire [15:0] _000, _001, _6_bit_ext__16_bit_immed, _7_bit_ext__16_bit_ascii_value, _010, _011, _100, _101,
       _110, _111, _128_binary__128_binary, alu_1_output_data, Combine_4_12_target_address,
       multiplexer_3_out, multiplexer_4_out, multiplexer_5_out, multiplexer_6_out, multiplexer_7_out,
       multiplexer_8_out, multiplexer_9_out, multiplexer_10_out, PC_1, PC_1_Imm_output, PC_output, plus_1,
       ram_1_data, regfile_rs_data, regfile_rt_data, rom_1_data;

  PC___1 pc_1_1 (.PC_1(plus_1));
  // Probe on _000
  // Probe on _001
  // Probe on _010
  // Probe on _011
  // Probe on _100
  // Probe on _101
  // Probe on _110
  // Probe on _111
  PC PC (.Reset(reset), .clk(Clock), .writeEnable(1'b1), .Input(multiplexer_6_out), .Output(PC_output));
  _16_bit_adder PC_PC_1 (.rs_Data(PC_output), .rt_Data(plus_1), .Sub(1'b0), .Output(PC_1));  // open: ovf
  ROM #(.addrWidth(16), .dataWidth(16)) rom_1 (.addr(PC_output), .data(rom_1_data));  // open: sel
  Clock clock_1 (.out(Clock));
  Top_4_PC_bits Top_4_PC_bits (.PC(PC_output), .Top_4_PC_bits(Top_4_PC_bits_top_4_pc_bits));
  RegisterFile regfile (
    .WriteReg(multiplexer_10_out), .Clock(Clock), .writeEnabled(Rwe), .WriteReg_2(multiplexer_1_out),
    .Reset(reset), .rs_Data(regfile_rs_data), .rs(Rs), .rt(Rt), .rt_Data(regfile_rt_data), .r0(_000),
    .r1(_001), .r2(_010), .r3(_011), .r4(_100), .r5(_101), .r6(_110), .r7(_111));
  Multiplexer #(.width(3), .enable("false")) multiplexer_1 (
    .in0(multiplexer_2_out), .in1(r7_1_r7), .out(multiplexer_1_out), .sel(JAL));
  Multiplexer #(.width(3), .enable("false")) multiplexer_2 (.in0(Rd), .in1(Rt), .out(multiplexer_2_out), .sel(Rdst));
  Control_Signal control_signal_1 (
    .Instruction(rom_1_data), .BR(BR), .JP(JP), .ALUinB(ALUinB), .ALUop(ALUop), .DMwe(DMwe), .Rwe(Rwe),
    .Rdst(Rdst), .Rwd(Rwd), .JR(JR), .JAL(JAL), .TTYenable(TTYenable), .KBenable(KBenable));
  r7 r7_1 (.r7(r7_1_r7));
  Instruction_Breakdown Instruction_Breakdown (
    .Instruction(rom_1_data), .Rs(Rs), .Rt(Rt), .Rd(Rd), .shamt(shamt), .Immediate(Immediate),
    .Address(Address), .opcode(opcode));
  Combine_4_12_bits Combine_4_12 (
    .Immed_Address(Address), .Top_4_PC_bits(Top_4_PC_bits_top_4_pc_bits),
    .Target_Address(Combine_4_12_target_address));
  Multiplexer #(.width(16), .enable("false")) multiplexer_3 (
    .in0(regfile_rt_data), .in1(_6_bit_ext__16_bit_immed), .out(multiplexer_3_out), .sel(ALUinB));
  _6_bit_Sign_Ext _6_bit_ext (._6_bit_Immed(Immediate), ._16_bit_Immed(_6_bit_ext__16_bit_immed));
  _16_bit_adder PC_1_Imm (
    .rs_Data(PC_1), .rt_Data(_6_bit_ext__16_bit_immed), .Sub(1'b0), .Output(PC_1_Imm_output));  // open: ovf
  ALU alu_1 (
    .rs_Data(regfile_rs_data), .rt_Data(multiplexer_3_out), .shamt(shamt), .Output_Data(alu_1_output_data),
    .ALUop(ALUop), .Output_Branch(alu_1_output_branch));
  and branch (branch_out, BR, alu_1_output_branch);
  _7_bit__rs _7_bit__rs (.rs_Data(alu_1_output_data), ._7_bit__rs(_7_bit__rs__7_bit__rs));
  TTY #(.rows(13), .cols(80), .trigger("falling")) tty_1 (
    .data(_7_bit__rs__7_bit__rs), .clk(Clock), .we(TTYenable), .clr(reset));
  Multiplexer #(.width(16), .enable("false")) multiplexer_4 (
    .in0(PC_1), .in1(PC_1_Imm_output), .out(multiplexer_4_out), .sel(branch_out));
  or or_1 (or_1_out, JP, JAL);
  not not_1 (not_1_out, Clock);
  Keyboard keyboard_1 (.clk(Clock), .re(KBenable), .clr(reset), .data(keyboard_1_data));  // open: avail
  Multiplexer #(.width(16), .enable("false")) multiplexer_5 (
    .in0(multiplexer_4_out), .in1(Combine_4_12_target_address), .out(multiplexer_5_out), .sel(or_1_out));
  RAM #(.addrWidth(16), .dataWidth(16), .bus("separate")) ram_1 (
    .addr(alu_1_output_data), .din(regfile_rt_data), .data(ram_1_data), .str(DMwe), .clk(not_1_out),
    .clr(ResetMem));  // open: sel, ld
  Multiplexer #(.width(16), .enable("false")) multiplexer_6 (
    .in0(multiplexer_5_out), .in1(alu_1_output_data), .out(multiplexer_6_out), .sel(JR));
  Multiplexer #(.width(16), .enable("false")) multiplexer_7 (
    .in0(alu_1_output_data), .in1(ram_1_data), .out(multiplexer_7_out), .sel(Rwd));
  _7_bit_Zero_Extender _7_bit_ext (
    ._7_bit_ASCII_Value(keyboard_1_data), ._16_bit_ASCII_value(_7_bit_ext__16_bit_ascii_value));
  _128_binary _128_binary (._128_binary(_128_binary__128_binary));
  Multiplexer #(.width(16), .enable("false")) multiplexer_8 (
    .in0(multiplexer_7_out), .in1(PC_1), .out(multiplexer_8_out), .sel(JAL));
  Multiplexer #(.width(16), .enable("false")) multiplexer_9 (
    .in0(_7_bit_ext__16_bit_ascii_value), .in1(_128_binary__128_binary), .out(multiplexer_9_out),
    .sel(beqz_1_beqz__rs));
  BEQZ beqz_1 (.rs_Data(_7_bit_ext__16_bit_ascii_value), .beqz__rs(beqz_1_beqz__rs));
  Multiplexer #(.width(16), .enable("false")) multiplexer_10 (
    .in0(multiplexer_8_out), .in1(multiplexer_9_out), .out(multiplexer_10_out), .sel(KBenable));

  // Notes on the sheet:
  //   contents of rom_1 (hex, n*v repeats v):
  //   2050 209f 3458 2070 2090 4458 803f
endmodule

module _1_bit_adder (
  input  Cin,
  input  A,
  input  B,
  output result,
  output Cout
);

  wire and_1_out, and_2_out, xor_1_out;

  and and_1 (and_1_out, B, A);
  xor xor_1 (xor_1_out, A, B);
  or or_1 (Cout, and_1_out, and_2_out);
  and and_2 (and_2_out, xor_1_out, Cin);
  xor xor_2 (result, Cin, xor_1_out);
endmodule

module _16_bit_adder (
  input  Sub,
  input  [15:0] rs_Data,
  input  [15:0] rt_Data,
  output [15:0] Output,
  output ovf
);

  wire n1_bit_adder_1_cout, n1_bit_adder_2_cout, n1_bit_adder_3_cout, n1_bit_adder_4_cout,
       n1_bit_adder_5_cout, n1_bit_adder_6_cout, n1_bit_adder_7_cout, n1_bit_adder_8_cout,
       n1_bit_adder_9_cout, n1_bit_adder_10_cout, n1_bit_adder_11_cout, n1_bit_adder_12_cout,
       n1_bit_adder_13_cout, n1_bit_adder_14_cout, n1_bit_adder_15_cout, n1_bit_adder_16_cout, xor_1_out,
       xor_2_out, xor_3_out, xor_4_out, xor_5_out, xor_6_out, xor_7_out, xor_8_out, xor_9_out, xor_10_out,
       xor_11_out, xor_12_out, xor_13_out, xor_14_out, xor_15_out, xor_16_out;

  xor xor_1 (xor_1_out, rt_Data[0], Sub);
  xor xor_2 (xor_2_out, rt_Data[1], Sub);
  xor xor_3 (xor_3_out, rt_Data[2], Sub);
  xor xor_4 (xor_4_out, rt_Data[3], Sub);
  xor xor_5 (xor_5_out, rt_Data[4], Sub);
  xor xor_6 (xor_6_out, rt_Data[5], Sub);
  xor xor_7 (xor_7_out, rt_Data[6], Sub);
  xor xor_8 (xor_8_out, rt_Data[7], Sub);
  xor xor_9 (xor_9_out, rt_Data[8], Sub);
  xor xor_10 (xor_10_out, rt_Data[9], Sub);
  xor xor_11 (xor_11_out, rt_Data[10], Sub);
  xor xor_12 (xor_12_out, rt_Data[11], Sub);
  xor xor_13 (xor_13_out, rt_Data[12], Sub);
  xor xor_14 (xor_14_out, rt_Data[13], Sub);
  xor xor_15 (xor_15_out, rt_Data[14], Sub);
  xor xor_16 (xor_16_out, rt_Data[15], Sub);
  _1_bit_adder u_1_bit_adder_1 (
    .A(xor_1_out), .B(rs_Data[0]), .Cin(Sub), .Cout(n1_bit_adder_1_cout), .result(Output[0]));
  _1_bit_adder u_1_bit_adder_2 (
    .A(xor_2_out), .B(rs_Data[1]), .Cin(n1_bit_adder_1_cout), .Cout(n1_bit_adder_2_cout), .result(Output[1]));
  _1_bit_adder u_1_bit_adder_3 (
    .A(xor_3_out), .B(rs_Data[2]), .Cin(n1_bit_adder_2_cout), .Cout(n1_bit_adder_3_cout), .result(Output[2]));
  _1_bit_adder u_1_bit_adder_4 (
    .A(xor_4_out), .B(rs_Data[3]), .Cin(n1_bit_adder_3_cout), .Cout(n1_bit_adder_4_cout), .result(Output[3]));
  _1_bit_adder u_1_bit_adder_5 (
    .A(xor_5_out), .B(rs_Data[4]), .Cin(n1_bit_adder_4_cout), .Cout(n1_bit_adder_5_cout), .result(Output[4]));
  _1_bit_adder u_1_bit_adder_6 (
    .A(xor_6_out), .B(rs_Data[5]), .Cin(n1_bit_adder_5_cout), .Cout(n1_bit_adder_6_cout), .result(Output[5]));
  _1_bit_adder u_1_bit_adder_7 (
    .A(xor_7_out), .B(rs_Data[6]), .Cin(n1_bit_adder_6_cout), .Cout(n1_bit_adder_7_cout), .result(Output[6]));
  _1_bit_adder u_1_bit_adder_8 (
    .A(xor_8_out), .B(rs_Data[7]), .Cin(n1_bit_adder_7_cout), .Cout(n1_bit_adder_8_cout), .result(Output[7]));
  _1_bit_adder u_1_bit_adder_9 (
    .A(xor_9_out), .B(rs_Data[8]), .Cin(n1_bit_adder_8_cout), .Cout(n1_bit_adder_9_cout), .result(Output[8]));
  _1_bit_adder u_1_bit_adder_10 (
    .A(xor_10_out), .B(rs_Data[9]), .Cin(n1_bit_adder_9_cout), .Cout(n1_bit_adder_10_cout), .result(Output[9]));
  _1_bit_adder u_1_bit_adder_11 (
    .A(xor_11_out), .B(rs_Data[10]), .Cin(n1_bit_adder_10_cout), .Cout(n1_bit_adder_11_cout),
    .result(Output[10]));
  _1_bit_adder u_1_bit_adder_12 (
    .A(xor_12_out), .B(rs_Data[11]), .Cin(n1_bit_adder_11_cout), .Cout(n1_bit_adder_12_cout),
    .result(Output[11]));
  _1_bit_adder u_1_bit_adder_13 (
    .A(xor_13_out), .B(rs_Data[12]), .Cin(n1_bit_adder_12_cout), .Cout(n1_bit_adder_13_cout),
    .result(Output[12]));
  _1_bit_adder u_1_bit_adder_14 (
    .A(xor_14_out), .B(rs_Data[13]), .Cin(n1_bit_adder_13_cout), .Cout(n1_bit_adder_14_cout),
    .result(Output[13]));
  _1_bit_adder u_1_bit_adder_15 (
    .A(xor_15_out), .B(rs_Data[14]), .Cin(n1_bit_adder_14_cout), .Cout(n1_bit_adder_15_cout),
    .result(Output[14]));
  _1_bit_adder u_1_bit_adder_16 (
    .A(xor_16_out), .B(rs_Data[15]), .Cin(n1_bit_adder_15_cout), .Cout(n1_bit_adder_16_cout),
    .result(Output[15]));
  xor xor_17 (ovf, n1_bit_adder_16_cout, n1_bit_adder_15_cout);

  // Other names for the same wires on the sheet: Rs_0 = rs_Data[0]; Rs_1 = rs_Data[1]; Rs_2 = rs_Data[2];
  //   Rs_3 = rs_Data[3]; Rs_4 = rs_Data[4]; Rs_5 = rs_Data[5]; Rs_6 = rs_Data[6]; Rs_7 = rs_Data[7];
  //   Rs_8 = rs_Data[8]; Rs_9 = rs_Data[9]; Rs_10 = rs_Data[10]; Rs_11 = rs_Data[11]; Rs_12 = rs_Data[12];
  //   Rs_13 = rs_Data[13]; Rs_14 = rs_Data[14]; Rs_15 = rs_Data[15]; Rt_0 = rt_Data[0]; Rt_1 = rt_Data[1];
  //   Rt_2 = rt_Data[2]; Rt_3 = rt_Data[3]; Rt_4 = rt_Data[4]; Rt_5 = rt_Data[5]; Rt_6 = rt_Data[6];
  //   Rt_7 = rt_Data[7]; Rt_8 = rt_Data[8]; Rt_9 = rt_Data[9]; Rt_10 = rt_Data[10]; Rt_11 = rt_Data[11];
  //   Rt_12 = rt_Data[12]; Rt_13 = rt_Data[13]; Rt_14 = rt_Data[14]; Rt_15 = rt_Data[15]
endmodule

module _16_bit_Register (
  input  Reset,
  input  clk,
  input  writeEnable,
  input  [15:0] Input,
  output [15:0] Output
);

  D_Flip_Flop #(.trigger("falling")) d_ff_1 (
    .clk(clk), .D(Input[0]), .Q(Output[0]), .en(writeEnable), .reset(Reset));  // open: Qn, preset
  D_Flip_Flop #(.trigger("falling")) d_ff_2 (
    .clk(clk), .D(Input[1]), .Q(Output[1]), .en(writeEnable), .reset(Reset));  // open: Qn, preset
  D_Flip_Flop #(.trigger("falling")) d_ff_3 (
    .clk(clk), .D(Input[2]), .Q(Output[2]), .en(writeEnable), .reset(Reset));  // open: Qn, preset
  D_Flip_Flop #(.trigger("falling")) d_ff_4 (
    .clk(clk), .D(Input[3]), .Q(Output[3]), .en(writeEnable), .reset(Reset));  // open: Qn, preset
  D_Flip_Flop #(.trigger("falling")) d_ff_5 (
    .clk(clk), .D(Input[4]), .Q(Output[4]), .en(writeEnable), .reset(Reset));  // open: Qn, preset
  D_Flip_Flop #(.trigger("falling")) d_ff_6 (
    .clk(clk), .D(Input[5]), .Q(Output[5]), .en(writeEnable), .reset(Reset));  // open: Qn, preset
  D_Flip_Flop #(.trigger("falling")) d_ff_7 (
    .clk(clk), .D(Input[6]), .Q(Output[6]), .en(writeEnable), .reset(Reset));  // open: Qn, preset
  D_Flip_Flop #(.trigger("falling")) d_ff_8 (
    .clk(clk), .D(Input[7]), .Q(Output[7]), .en(writeEnable), .reset(Reset));  // open: Qn, preset
  D_Flip_Flop #(.trigger("falling")) d_ff_9 (
    .clk(clk), .D(Input[8]), .Q(Output[8]), .en(writeEnable), .reset(Reset));  // open: Qn, preset
  D_Flip_Flop #(.trigger("falling")) d_ff_10 (
    .clk(clk), .D(Input[9]), .Q(Output[9]), .en(writeEnable), .reset(Reset));  // open: Qn, preset
  D_Flip_Flop #(.trigger("falling")) d_ff_11 (
    .clk(clk), .D(Input[10]), .Q(Output[10]), .en(writeEnable), .reset(Reset));  // open: Qn, preset
  D_Flip_Flop #(.trigger("falling")) d_ff_12 (
    .clk(clk), .D(Input[11]), .Q(Output[11]), .en(writeEnable), .reset(Reset));  // open: Qn, preset
  D_Flip_Flop #(.trigger("falling")) d_ff_13 (
    .clk(clk), .D(Input[12]), .Q(Output[12]), .en(writeEnable), .reset(Reset));  // open: Qn, preset
  D_Flip_Flop #(.trigger("falling")) d_ff_14 (
    .clk(clk), .D(Input[13]), .Q(Output[13]), .en(writeEnable), .reset(Reset));  // open: Qn, preset
  D_Flip_Flop #(.trigger("falling")) d_ff_15 (
    .clk(clk), .D(Input[14]), .Q(Output[14]), .en(writeEnable), .reset(Reset));  // open: Qn, preset
  D_Flip_Flop #(.trigger("falling")) d_ff_16 (
    .clk(clk), .D(Input[15]), .Q(Output[15]), .en(writeEnable), .reset(Reset));  // open: Qn, preset
endmodule

module RegisterFile (
  input  [15:0] WriteReg,
  input  Reset,
  input  Clock,
  input  writeEnabled,
  input  [2:0] rs,
  input  [2:0] WriteReg_2,
  input  [2:0] rt,
  output [15:0] r0,
  output [15:0] r1,
  output [15:0] rs_Data,
  output [15:0] r2,
  output [15:0] r3,
  output [15:0] r4,
  output [15:0] rt_Data,
  output [15:0] r5,
  output [15:0] r6,
  output [15:0] r7
);

  wire and_2_out, and_3_out, and_4_out, and_5_out, and_6_out, and_7_out, and_8_out, n3_8_decoder_1__000,
       n3_8_decoder_1__001, n3_8_decoder_1__010, n3_8_decoder_1__011, n3_8_decoder_1__100,
       n3_8_decoder_1__101, n3_8_decoder_1__110, n3_8_decoder_1__111;

  _3_8_Decoder u_3_8_decoder_1 (
    .WriteReg(WriteReg_2), ._000(n3_8_decoder_1__000), ._001(n3_8_decoder_1__001),
    ._010(n3_8_decoder_1__010), ._011(n3_8_decoder_1__011), ._100(n3_8_decoder_1__100),
    ._101(n3_8_decoder_1__101), ._110(n3_8_decoder_1__110), ._111(n3_8_decoder_1__111));
  // AND_Gate and_1 has open pins: in0=writeEnabled, in1=n3_8_decoder_1__000, out=open
  and and_2 (and_2_out, writeEnabled, n3_8_decoder_1__001);
  and and_3 (and_3_out, writeEnabled, n3_8_decoder_1__010);
  and and_4 (and_4_out, writeEnabled, n3_8_decoder_1__011);
  and and_5 (and_5_out, writeEnabled, n3_8_decoder_1__100);
  and and_6 (and_6_out, writeEnabled, n3_8_decoder_1__101);
  and and_7 (and_7_out, writeEnabled, n3_8_decoder_1__110);
  and and_8 (and_8_out, writeEnabled, n3_8_decoder_1__111);
  _16_bit_Register u_16_bit_register_1 (.Reset(Reset), .clk(Clock), .writeEnable(1'b0), .Input(WriteReg), .Output(r0));
  _16_bit_Register u_16_bit_register_2 (
    .Reset(Reset), .clk(Clock), .writeEnable(and_2_out), .Input(WriteReg), .Output(r1));
  _16_bit_Register u_16_bit_register_3 (
    .Reset(Reset), .clk(Clock), .writeEnable(and_3_out), .Input(WriteReg), .Output(r2));
  _16_bit_Register u_16_bit_register_4 (
    .Reset(Reset), .clk(Clock), .writeEnable(and_4_out), .Input(WriteReg), .Output(r3));
  _16_bit_Register u_16_bit_register_5 (
    .Reset(Reset), .clk(Clock), .writeEnable(and_5_out), .Input(WriteReg), .Output(r4));
  _16_bit_Register u_16_bit_register_6 (
    .Reset(Reset), .clk(Clock), .writeEnable(and_6_out), .Input(WriteReg), .Output(r5));
  _16_bit_Register u_16_bit_register_7 (
    .Reset(Reset), .clk(Clock), .writeEnable(and_7_out), .Input(WriteReg), .Output(r6));
  _16_bit_Register u_16_bit_register_8 (
    .Reset(Reset), .clk(Clock), .writeEnable(and_8_out), .Input(WriteReg), .Output(r7));
  Multiplexer #(.select(3), .width(16), .enable("false")) multiplexer_1 (
    .in0(r0), .in1(r1), .in2(r2), .in3(r3), .in4(r4), .in5(r5), .in6(r6), .in7(r7), .out(rs_Data), .sel(rs));
  Multiplexer #(.select(3), .width(16), .enable("false")) multiplexer_2 (
    .in0(r0), .in1(r1), .in2(r2), .in3(r3), .in4(r4), .in5(r5), .in6(r6), .in7(r7), .out(rt_Data), .sel(rt));

  // Other names for the same wires on the sheet: _000[15:0] = r0; _001[15:0] = r1; _010[15:0] = r2; _011[15:0] = r3;
  //   _100[15:0] = r4; _101[15:0] = r5; _110[15:0] = r6; _111[15:0] = r7
endmodule

module _3_8_Decoder (
  input  [2:0] WriteReg,
  output _000,
  output _001,
  output _010,
  output _011,
  output _100,
  output _101,
  output _110,
  output _111
);

  wire n0, n1, n2;

  not not_1 (n0, WriteReg[0]);
  not not_2 (n1, WriteReg[1]);
  not not_3 (n2, WriteReg[2]);
  and and_1 (_000, n0, n1, n2);
  and and_2 (_001, WriteReg[0], n1, n2);
  and and_3 (_010, n0, WriteReg[1], n2);
  and and_4 (_011, WriteReg[0], WriteReg[1], n2);
  and and_5 (_100, n0, n1, WriteReg[2]);
  and and_6 (_101, WriteReg[0], n1, WriteReg[2]);
  and and_7 (_110, n0, WriteReg[1], WriteReg[2]);
  and and_8 (_111, WriteReg[0], WriteReg[1], WriteReg[2]);

  // Other names for the same wires on the sheet: _0 = WriteReg[0]; _1 = WriteReg[1]; _2 = WriteReg[2]
endmodule

module BGT__rs____rt (
  input  [15:0] rs_Data,
  input  [15:0] rt_Data,
  output rs____rt
);

  wire n16_bit_adder_1_ovf, or_1_out, xnor_1_out;
  wire [15:0] n16_bit_adder_1_output;

  _16_bit_adder u_16_bit_adder_1 (
    .rs_Data(rs_Data), .rt_Data(rt_Data), .Sub(1'b1), .Output(n16_bit_adder_1_output),
    .ovf(n16_bit_adder_1_ovf));
  or or_1 (or_1_out, n16_bit_adder_1_output[0], n16_bit_adder_1_output[1], n16_bit_adder_1_output[2], n16_bit_adder_1_output[3], n16_bit_adder_1_output[4], n16_bit_adder_1_output[5], n16_bit_adder_1_output[6], n16_bit_adder_1_output[7], n16_bit_adder_1_output[8], n16_bit_adder_1_output[9], n16_bit_adder_1_output[10], n16_bit_adder_1_output[11], n16_bit_adder_1_output[12], n16_bit_adder_1_output[13], n16_bit_adder_1_output[14], n16_bit_adder_1_output[15]);
  xnor xnor_1 (xnor_1_out, n16_bit_adder_1_output[15], n16_bit_adder_1_ovf);
  and and_1 (rs____rt, or_1_out, xnor_1_out);
endmodule

module Control_Signal (
  input  [15:0] Instruction,
  output BR,
  output JP,
  output ALUinB,
  output [3:0] ALUop,
  output DMwe,
  output Rwe,
  output Rdst,
  output Rwd,
  output JR,
  output JAL,
  output TTYenable,
  output KBenable
);

  wire add, addi, beqz, bgt, \nand , shl, shra, sub, \xor ;

  ALUop_Control_Bus aluop_control_bus_1 (
    .\nand (\nand ), .\xor (\xor ), .addi(addi), .add(add), .sub(sub), .shra(shra), .shl(shl), .bgt(bgt),
    .beqz(beqz), .lw(Rwd), .sw(DMwe), .j(JP), .jr(JR), .jal(JAL), .\output (TTYenable), .\input (KBenable),
    .ALUop(ALUop));
  _4_16_Decoder u_4_16_decoder_1 (
    .opcode(Instruction[15:12]), ._0000_nand(\nand ), ._0001_xor(\xor ), ._0010_addi(addi), ._0011_add(add),
    ._0100_sub(sub), ._0101_shra(shra), ._0110_shl(shl), ._0111_bgt(bgt), ._1000_beqz(beqz), ._1001_lw(Rwd),
    ._1010_sw(DMwe), ._1011_j(JP), ._1100_jr(JR), ._1101_jal(JAL), ._1110_output(TTYenable),
    ._1111_input(KBenable));
  or or_1 (BR, bgt, beqz);
  or or_2 (ALUinB, addi, Rwd, DMwe);
  or or_3 (Rwe, \nand , \xor , addi, add, Rwd, sub, shra, shl, KBenable, JAL);
  or or_4 (Rdst, addi, Rwd);

  // Other names for the same wires on the sheet: input = KBenable; j = JP; lw = Rwd; output = TTYenable; sw = DMwe
endmodule

module _4_16_Decoder (
  input  [3:0] opcode,
  output _0000_nand,
  output _0001_xor,
  output _0010_addi,
  output _0011_add,
  output _0100_sub,
  output _0101_shra,
  output _0110_shl,
  output _0111_bgt,
  output _1000_beqz,
  output _1001_lw,
  output _1010_sw,
  output _1011_j,
  output _1100_jr,
  output _1101_jal,
  output _1110_output,
  output _1111_input
);

  wire n0, n1, n2, n3;

  not not_1 (n0, opcode[0]);
  not not_2 (n1, opcode[1]);
  not not_3 (n2, opcode[2]);
  not not_4 (n3, opcode[3]);
  and and_1 (_0000_nand, n0, n1, n2, n3);
  and and_2 (_0001_xor, opcode[0], n1, n2, n3);
  and and_3 (_0010_addi, n0, opcode[1], n2, n3);
  and and_4 (_0011_add, opcode[0], opcode[1], n2, n3);
  and and_5 (_0100_sub, n0, n1, opcode[2], n3);
  and and_6 (_0101_shra, opcode[0], n1, opcode[2], n3);
  and and_7 (_0110_shl, n0, opcode[1], opcode[2], n3);
  and and_8 (_0111_bgt, opcode[0], opcode[1], opcode[2], n3);
  and and_9 (_1000_beqz, n0, n1, n2, opcode[3]);
  and and_10 (_1001_lw, opcode[0], n1, n2, opcode[3]);
  and and_11 (_1010_sw, n0, opcode[1], n2, opcode[3]);
  and and_12 (_1011_j, opcode[0], opcode[1], n2, opcode[3]);
  and and_13 (_1100_jr, n0, n1, opcode[2], opcode[3]);
  and and_14 (_1101_jal, opcode[0], n1, opcode[2], opcode[3]);
  and and_15 (_1110_output, n0, opcode[1], opcode[2], opcode[3]);
  and and_16 (_1111_input, opcode[0], opcode[1], opcode[2], opcode[3]);

  // Other names for the same wires on the sheet: _0 = opcode[0]; _1 = opcode[1]; _2 = opcode[2]; _3 = opcode[3]
endmodule

module Left_Shift (
  input  [15:0] rs_Data,
  input  [2:0] shamt,
  output [15:0] rd_Data
);

  wire multiplexer_1_out, multiplexer_2_out, multiplexer_3_out, multiplexer_4_out, multiplexer_5_out,
       multiplexer_6_out, multiplexer_7_out, multiplexer_8_out, multiplexer_9_out, multiplexer_10_out,
       multiplexer_11_out, multiplexer_12_out, multiplexer_13_out, multiplexer_14_out, multiplexer_15_out,
       multiplexer_16_out, multiplexer_17_out, multiplexer_18_out, multiplexer_19_out, multiplexer_20_out,
       multiplexer_21_out, multiplexer_22_out, multiplexer_23_out, multiplexer_25_out, multiplexer_26_out,
       multiplexer_27_out, multiplexer_31_out, multiplexer_32_out, multiplexer_33_out, multiplexer_36_out,
       multiplexer_37_out, multiplexer_41_out;

  Multiplexer #(.enable("false")) multiplexer_1 (
    .in0(rs_Data[15]), .in1(rs_Data[14]), .out(multiplexer_1_out), .sel(shamt[0]));
  Multiplexer #(.enable("false")) multiplexer_2 (
    .in0(rs_Data[14]), .in1(rs_Data[13]), .out(multiplexer_2_out), .sel(shamt[0]));
  Multiplexer #(.enable("false")) multiplexer_3 (
    .in0(rs_Data[13]), .in1(rs_Data[12]), .out(multiplexer_3_out), .sel(shamt[0]));
  Multiplexer #(.enable("false")) multiplexer_4 (
    .in0(rs_Data[12]), .in1(rs_Data[11]), .out(multiplexer_4_out), .sel(shamt[0]));
  Multiplexer #(.enable("false")) multiplexer_5 (
    .in0(rs_Data[11]), .in1(rs_Data[10]), .out(multiplexer_5_out), .sel(shamt[0]));
  Multiplexer #(.enable("false")) multiplexer_6 (
    .in0(rs_Data[10]), .in1(rs_Data[9]), .out(multiplexer_6_out), .sel(shamt[0]));
  Multiplexer #(.enable("false")) multiplexer_7 (
    .in0(rs_Data[9]), .in1(rs_Data[8]), .out(multiplexer_7_out), .sel(shamt[0]));
  Multiplexer #(.enable("false")) multiplexer_8 (
    .in0(rs_Data[8]), .in1(rs_Data[7]), .out(multiplexer_8_out), .sel(shamt[0]));
  Multiplexer #(.enable("false")) multiplexer_9 (
    .in0(multiplexer_1_out), .in1(multiplexer_3_out), .out(multiplexer_9_out), .sel(shamt[1]));
  Multiplexer #(.enable("false")) multiplexer_10 (
    .in0(multiplexer_2_out), .in1(multiplexer_4_out), .out(multiplexer_10_out), .sel(shamt[1]));
  Multiplexer #(.enable("false")) multiplexer_11 (
    .in0(rs_Data[7]), .in1(rs_Data[6]), .out(multiplexer_11_out), .sel(shamt[0]));
  Multiplexer #(.enable("false")) multiplexer_12 (
    .in0(rs_Data[6]), .in1(rs_Data[5]), .out(multiplexer_12_out), .sel(shamt[0]));
  Multiplexer #(.enable("false")) multiplexer_13 (
    .in0(multiplexer_3_out), .in1(multiplexer_5_out), .out(multiplexer_13_out), .sel(shamt[1]));
  Multiplexer #(.enable("false")) multiplexer_14 (
    .in0(multiplexer_4_out), .in1(multiplexer_6_out), .out(multiplexer_14_out), .sel(shamt[1]));
  Multiplexer #(.enable("false")) multiplexer_15 (
    .in0(multiplexer_5_out), .in1(multiplexer_7_out), .out(multiplexer_15_out), .sel(shamt[1]));
  Multiplexer #(.enable("false")) multiplexer_16 (
    .in0(rs_Data[5]), .in1(rs_Data[4]), .out(multiplexer_16_out), .sel(shamt[0]));
  Multiplexer #(.enable("false")) multiplexer_17 (
    .in0(rs_Data[4]), .in1(rs_Data[3]), .out(multiplexer_17_out), .sel(shamt[0]));
  Multiplexer #(.enable("false")) multiplexer_18 (
    .in0(rs_Data[3]), .in1(rs_Data[2]), .out(multiplexer_18_out), .sel(shamt[0]));
  Multiplexer #(.enable("false")) multiplexer_19 (
    .in0(multiplexer_6_out), .in1(multiplexer_8_out), .out(multiplexer_19_out), .sel(shamt[1]));
  Multiplexer #(.enable("false")) multiplexer_20 (
    .in0(multiplexer_7_out), .in1(multiplexer_11_out), .out(multiplexer_20_out), .sel(shamt[1]));
  Multiplexer #(.enable("false")) multiplexer_21 (
    .in0(rs_Data[2]), .in1(rs_Data[1]), .out(multiplexer_21_out), .sel(shamt[0]));
  Multiplexer #(.enable("false")) multiplexer_22 (
    .in0(rs_Data[1]), .in1(rs_Data[0]), .out(multiplexer_22_out), .sel(shamt[0]));
  Multiplexer #(.enable("false")) multiplexer_23 (
    .in0(rs_Data[0]), .in1(1'b0), .out(multiplexer_23_out), .sel(shamt[0]));
  Multiplexer #(.enable("false")) multiplexer_24 (
    .in0(multiplexer_9_out), .in1(multiplexer_15_out), .out(rd_Data[15]), .sel(shamt[2]));
  Multiplexer #(.enable("false")) multiplexer_25 (
    .in0(multiplexer_8_out), .in1(multiplexer_12_out), .out(multiplexer_25_out), .sel(shamt[1]));
  Multiplexer #(.enable("false")) multiplexer_26 (
    .in0(multiplexer_11_out), .in1(multiplexer_16_out), .out(multiplexer_26_out), .sel(shamt[1]));
  Multiplexer #(.enable("false")) multiplexer_27 (
    .in0(multiplexer_12_out), .in1(multiplexer_17_out), .out(multiplexer_27_out), .sel(shamt[1]));
  Multiplexer #(.enable("false")) multiplexer_28 (
    .in0(multiplexer_10_out), .in1(multiplexer_19_out), .out(rd_Data[14]), .sel(shamt[2]));
  Multiplexer #(.enable("false")) multiplexer_29 (
    .in0(multiplexer_13_out), .in1(multiplexer_20_out), .out(rd_Data[13]), .sel(shamt[2]));
  Multiplexer #(.enable("false")) multiplexer_30 (
    .in0(multiplexer_14_out), .in1(multiplexer_25_out), .out(rd_Data[12]), .sel(shamt[2]));
  Multiplexer #(.enable("false")) multiplexer_31 (
    .in0(multiplexer_16_out), .in1(multiplexer_18_out), .out(multiplexer_31_out), .sel(shamt[1]));
  Multiplexer #(.enable("false")) multiplexer_32 (
    .in0(multiplexer_17_out), .in1(multiplexer_21_out), .out(multiplexer_32_out), .sel(shamt[1]));
  Multiplexer #(.enable("false")) multiplexer_33 (
    .in0(multiplexer_18_out), .in1(multiplexer_22_out), .out(multiplexer_33_out), .sel(shamt[1]));
  Multiplexer #(.enable("false")) multiplexer_34 (
    .in0(multiplexer_15_out), .in1(multiplexer_26_out), .out(rd_Data[11]), .sel(shamt[2]));
  Multiplexer #(.enable("false")) multiplexer_35 (
    .in0(multiplexer_19_out), .in1(multiplexer_27_out), .out(rd_Data[10]), .sel(shamt[2]));
  Multiplexer #(.enable("false")) multiplexer_36 (
    .in0(multiplexer_21_out), .in1(multiplexer_23_out), .out(multiplexer_36_out), .sel(shamt[1]));
  Multiplexer #(.enable("false")) multiplexer_37 (
    .in0(multiplexer_22_out), .in1(1'b0), .out(multiplexer_37_out), .sel(shamt[1]));
  Multiplexer #(.enable("false")) multiplexer_38 (
    .in0(multiplexer_20_out), .in1(multiplexer_31_out), .out(rd_Data[9]), .sel(shamt[2]));
  Multiplexer #(.enable("false")) multiplexer_39 (
    .in0(multiplexer_25_out), .in1(multiplexer_32_out), .out(rd_Data[8]), .sel(shamt[2]));
  Multiplexer #(.enable("false")) multiplexer_40 (
    .in0(multiplexer_26_out), .in1(multiplexer_33_out), .out(rd_Data[7]), .sel(shamt[2]));
  Multiplexer #(.enable("false")) multiplexer_41 (
    .in0(multiplexer_23_out), .in1(1'b0), .out(multiplexer_41_out), .sel(shamt[1]));
  Multiplexer #(.enable("false")) multiplexer_42 (
    .in0(multiplexer_27_out), .in1(multiplexer_36_out), .out(rd_Data[6]), .sel(shamt[2]));
  Multiplexer #(.enable("false")) multiplexer_43 (
    .in0(multiplexer_31_out), .in1(multiplexer_37_out), .out(rd_Data[5]), .sel(shamt[2]));
  Multiplexer #(.enable("false")) multiplexer_44 (
    .in0(multiplexer_32_out), .in1(multiplexer_41_out), .out(rd_Data[4]), .sel(shamt[2]));
  Multiplexer #(.enable("false")) multiplexer_45 (
    .in0(multiplexer_33_out), .in1(1'b0), .out(rd_Data[3]), .sel(shamt[2]));
  Multiplexer #(.enable("false")) multiplexer_46 (
    .in0(multiplexer_36_out), .in1(1'b0), .out(rd_Data[2]), .sel(shamt[2]));
  Multiplexer #(.enable("false")) multiplexer_47 (
    .in0(multiplexer_37_out), .in1(1'b0), .out(rd_Data[1]), .sel(shamt[2]));
  Multiplexer #(.enable("false")) multiplexer_48 (
    .in0(multiplexer_41_out), .in1(1'b0), .out(rd_Data[0]), .sel(shamt[2]));
  _16_bit_adder u_16_bit_adder_1 ();  // open: rs_Data, rt_Data, Sub, Output, ovf

  // Other names for the same wires on the sheet: Rs_0 = rs_Data[0]; Rs_1 = rs_Data[1]; Rs_2 = rs_Data[2];
  //   Rs_3 = rs_Data[3]; Rs_4 = rs_Data[4]; Rs_5 = rs_Data[5]; Rs_6 = rs_Data[6]; Rs_7 = rs_Data[7];
  //   Rs_8 = rs_Data[8]; Rs_9 = rs_Data[9]; Rs_10 = rs_Data[10]; Rs_11 = rs_Data[11]; Rs_12 = rs_Data[12];
  //   Rs_13 = rs_Data[13]; Rs_14 = rs_Data[14]; Rs_15 = rs_Data[15]; shamt_0 = shamt[0]; shamt_1 = shamt[1];
  //   shamt_2 = shamt[2]
endmodule

module Right_Arith_Shift (
  input  [15:0] rs_Data,
  input  [2:0] shamt,
  output [15:0] rs_Data_2
);

  wire multiplexer_1_out, multiplexer_2_out, multiplexer_3_out, multiplexer_4_out, multiplexer_5_out,
       multiplexer_6_out, multiplexer_7_out, multiplexer_8_out, multiplexer_9_out, multiplexer_10_out,
       multiplexer_11_out, multiplexer_12_out, multiplexer_13_out, multiplexer_14_out, multiplexer_15_out,
       multiplexer_16_out, multiplexer_17_out, multiplexer_18_out, multiplexer_19_out, multiplexer_20_out,
       multiplexer_21_out, multiplexer_22_out, multiplexer_23_out, multiplexer_25_out, multiplexer_26_out,
       multiplexer_27_out, multiplexer_31_out, multiplexer_32_out, multiplexer_33_out, multiplexer_36_out,
       multiplexer_37_out, multiplexer_41_out;

  Multiplexer #(.enable("false")) multiplexer_1 (
    .in0(rs_Data[0]), .in1(rs_Data[1]), .out(multiplexer_1_out), .sel(shamt[0]));
  Multiplexer #(.enable("false")) multiplexer_2 (
    .in0(rs_Data[1]), .in1(rs_Data[2]), .out(multiplexer_2_out), .sel(shamt[0]));
  Multiplexer #(.enable("false")) multiplexer_3 (
    .in0(rs_Data[2]), .in1(rs_Data[3]), .out(multiplexer_3_out), .sel(shamt[0]));
  Multiplexer #(.enable("false")) multiplexer_4 (
    .in0(rs_Data[3]), .in1(rs_Data[4]), .out(multiplexer_4_out), .sel(shamt[0]));
  Multiplexer #(.enable("false")) multiplexer_5 (
    .in0(rs_Data[4]), .in1(rs_Data[5]), .out(multiplexer_5_out), .sel(shamt[0]));
  Multiplexer #(.enable("false")) multiplexer_6 (
    .in0(rs_Data[5]), .in1(rs_Data[6]), .out(multiplexer_6_out), .sel(shamt[0]));
  Multiplexer #(.enable("false")) multiplexer_7 (
    .in0(rs_Data[6]), .in1(rs_Data[7]), .out(multiplexer_7_out), .sel(shamt[0]));
  Multiplexer #(.enable("false")) multiplexer_8 (
    .in0(rs_Data[7]), .in1(rs_Data[8]), .out(multiplexer_8_out), .sel(shamt[0]));
  Multiplexer #(.enable("false")) multiplexer_9 (
    .in0(multiplexer_1_out), .in1(multiplexer_3_out), .out(multiplexer_9_out), .sel(shamt[1]));
  Multiplexer #(.enable("false")) multiplexer_10 (
    .in0(multiplexer_2_out), .in1(multiplexer_4_out), .out(multiplexer_10_out), .sel(shamt[1]));
  Multiplexer #(.enable("false")) multiplexer_11 (
    .in0(rs_Data[8]), .in1(rs_Data[9]), .out(multiplexer_11_out), .sel(shamt[0]));
  Multiplexer #(.enable("false")) multiplexer_12 (
    .in0(rs_Data[9]), .in1(rs_Data[10]), .out(multiplexer_12_out), .sel(shamt[0]));
  Multiplexer #(.enable("false")) multiplexer_13 (
    .in0(multiplexer_3_out), .in1(multiplexer_5_out), .out(multiplexer_13_out), .sel(shamt[1]));
  Multiplexer #(.enable("false")) multiplexer_14 (
    .in0(multiplexer_4_out), .in1(multiplexer_6_out), .out(multiplexer_14_out), .sel(shamt[1]));
  Multiplexer #(.enable("false")) multiplexer_15 (
    .in0(multiplexer_5_out), .in1(multiplexer_7_out), .out(multiplexer_15_out), .sel(shamt[1]));
  Multiplexer #(.enable("false")) multiplexer_16 (
    .in0(rs_Data[10]), .in1(rs_Data[11]), .out(multiplexer_16_out), .sel(shamt[0]));
  Multiplexer #(.enable("false")) multiplexer_17 (
    .in0(rs_Data[11]), .in1(rs_Data[12]), .out(multiplexer_17_out), .sel(shamt[0]));
  Multiplexer #(.enable("false")) multiplexer_18 (
    .in0(rs_Data[12]), .in1(rs_Data[13]), .out(multiplexer_18_out), .sel(shamt[0]));
  Multiplexer #(.enable("false")) multiplexer_19 (
    .in0(multiplexer_6_out), .in1(multiplexer_8_out), .out(multiplexer_19_out), .sel(shamt[1]));
  Multiplexer #(.enable("false")) multiplexer_20 (
    .in0(multiplexer_7_out), .in1(multiplexer_11_out), .out(multiplexer_20_out), .sel(shamt[1]));
  Multiplexer #(.enable("false")) multiplexer_21 (
    .in0(rs_Data[13]), .in1(rs_Data[14]), .out(multiplexer_21_out), .sel(shamt[0]));
  Multiplexer #(.enable("false")) multiplexer_22 (
    .in0(rs_Data[14]), .in1(rs_Data[15]), .out(multiplexer_22_out), .sel(shamt[0]));
  Multiplexer #(.enable("false")) multiplexer_23 (
    .in0(rs_Data[15]), .in1(rs_Data[15]), .out(multiplexer_23_out), .sel(shamt[0]));
  Multiplexer #(.enable("false")) multiplexer_24 (
    .in0(multiplexer_9_out), .in1(multiplexer_15_out), .out(rs_Data_2[0]), .sel(shamt[2]));
  Multiplexer #(.enable("false")) multiplexer_25 (
    .in0(multiplexer_8_out), .in1(multiplexer_12_out), .out(multiplexer_25_out), .sel(shamt[1]));
  Multiplexer #(.enable("false")) multiplexer_26 (
    .in0(multiplexer_11_out), .in1(multiplexer_16_out), .out(multiplexer_26_out), .sel(shamt[1]));
  Multiplexer #(.enable("false")) multiplexer_27 (
    .in0(multiplexer_12_out), .in1(multiplexer_17_out), .out(multiplexer_27_out), .sel(shamt[1]));
  Multiplexer #(.enable("false")) multiplexer_28 (
    .in0(multiplexer_10_out), .in1(multiplexer_19_out), .out(rs_Data_2[1]), .sel(shamt[2]));
  Multiplexer #(.enable("false")) multiplexer_29 (
    .in0(multiplexer_13_out), .in1(multiplexer_20_out), .out(rs_Data_2[2]), .sel(shamt[2]));
  Multiplexer #(.enable("false")) multiplexer_30 (
    .in0(multiplexer_14_out), .in1(multiplexer_25_out), .out(rs_Data_2[3]), .sel(shamt[2]));
  Multiplexer #(.enable("false")) multiplexer_31 (
    .in0(multiplexer_16_out), .in1(multiplexer_18_out), .out(multiplexer_31_out), .sel(shamt[1]));
  Multiplexer #(.enable("false")) multiplexer_32 (
    .in0(multiplexer_17_out), .in1(multiplexer_21_out), .out(multiplexer_32_out), .sel(shamt[1]));
  Multiplexer #(.enable("false")) multiplexer_33 (
    .in0(multiplexer_18_out), .in1(multiplexer_22_out), .out(multiplexer_33_out), .sel(shamt[1]));
  Multiplexer #(.enable("false")) multiplexer_34 (
    .in0(multiplexer_15_out), .in1(multiplexer_26_out), .out(rs_Data_2[4]), .sel(shamt[2]));
  Multiplexer #(.enable("false")) multiplexer_35 (
    .in0(multiplexer_19_out), .in1(multiplexer_27_out), .out(rs_Data_2[5]), .sel(shamt[2]));
  Multiplexer #(.enable("false")) multiplexer_36 (
    .in0(multiplexer_21_out), .in1(multiplexer_23_out), .out(multiplexer_36_out), .sel(shamt[1]));
  Multiplexer #(.enable("false")) multiplexer_37 (
    .in0(multiplexer_22_out), .in1(rs_Data[15]), .out(multiplexer_37_out), .sel(shamt[1]));
  Multiplexer #(.enable("false")) multiplexer_38 (
    .in0(multiplexer_20_out), .in1(multiplexer_31_out), .out(rs_Data_2[6]), .sel(shamt[2]));
  Multiplexer #(.enable("false")) multiplexer_39 (
    .in0(multiplexer_25_out), .in1(multiplexer_32_out), .out(rs_Data_2[7]), .sel(shamt[2]));
  Multiplexer #(.enable("false")) multiplexer_40 (
    .in0(multiplexer_26_out), .in1(multiplexer_33_out), .out(rs_Data_2[8]), .sel(shamt[2]));
  Multiplexer #(.enable("false")) multiplexer_41 (
    .in0(multiplexer_23_out), .in1(rs_Data[15]), .out(multiplexer_41_out), .sel(shamt[1]));
  Multiplexer #(.enable("false")) multiplexer_42 (
    .in0(multiplexer_27_out), .in1(multiplexer_36_out), .out(rs_Data_2[9]), .sel(shamt[2]));
  Multiplexer #(.enable("false")) multiplexer_43 (
    .in0(multiplexer_31_out), .in1(multiplexer_37_out), .out(rs_Data_2[10]), .sel(shamt[2]));
  Multiplexer #(.enable("false")) multiplexer_44 (
    .in0(multiplexer_32_out), .in1(multiplexer_41_out), .out(rs_Data_2[11]), .sel(shamt[2]));
  Multiplexer #(.enable("false")) multiplexer_45 (
    .in0(multiplexer_33_out), .in1(rs_Data[15]), .out(rs_Data_2[12]), .sel(shamt[2]));
  Multiplexer #(.enable("false")) multiplexer_46 (
    .in0(multiplexer_36_out), .in1(rs_Data[15]), .out(rs_Data_2[13]), .sel(shamt[2]));
  Multiplexer #(.enable("false")) multiplexer_47 (
    .in0(multiplexer_37_out), .in1(rs_Data[15]), .out(rs_Data_2[14]), .sel(shamt[2]));
  Multiplexer #(.enable("false")) multiplexer_48 (
    .in0(multiplexer_41_out), .in1(rs_Data[15]), .out(rs_Data_2[15]), .sel(shamt[2]));

  // Other names for the same wires on the sheet: rd_Data[15:0] = rs_Data_2; Rs_0 = rs_Data[0]; Rs_1 = rs_Data[1];
  //   Rs_2 = rs_Data[2]; Rs_3 = rs_Data[3]; Rs_4 = rs_Data[4]; Rs_5 = rs_Data[5]; Rs_6 = rs_Data[6];
  //   Rs_7 = rs_Data[7]; Rs_8 = rs_Data[8]; Rs_9 = rs_Data[9]; Rs_10 = rs_Data[10]; Rs_11 = rs_Data[11];
  //   Rs_12 = rs_Data[12]; Rs_13 = rs_Data[13]; Rs_14 = rs_Data[14]; Rs_15 = rs_Data[15]; shamt_0 = shamt[0];
  //   shamt_1 = shamt[1]; shamt_2 = shamt[2]
endmodule

module BEQZ (
  input  [15:0] rs_Data,
  output beqz__rs
);

  nor nor_1 (beqz__rs, rs_Data[0], rs_Data[1], rs_Data[2], rs_Data[3], rs_Data[4], rs_Data[5], rs_Data[6], rs_Data[7], rs_Data[8], rs_Data[9], rs_Data[10], rs_Data[11], rs_Data[12], rs_Data[13], rs_Data[14], rs_Data[15]);
endmodule

module Top_4_PC_bits (
  input  [15:0] PC,
  output [3:0] Top_4_PC_bits
);


  assign Top_4_PC_bits = PC[15:12];
endmodule

module Combine_4_12_bits (
  input  [11:0] Immed_Address,
  input  [3:0] Top_4_PC_bits,
  output [15:0] Target_Address
);


  assign Target_Address = {Top_4_PC_bits, Immed_Address};
endmodule

module _7_bit__rs (
  input  [15:0] rs_Data,
  output [6:0] _7_bit__rs
);


  assign _7_bit__rs = rs_Data[6:0];
endmodule

module ALUop_Control_Bus (
  input  \nand ,
  input  \xor ,
  input  addi,
  input  add,
  input  sub,
  input  shra,
  input  shl,
  input  bgt,
  input  beqz,
  input  lw,
  input  sw,
  input  j,
  input  jr,
  input  jal,
  input  \output ,
  input  \input ,
  output [3:0] ALUop
);

  or or_1 (ALUop[0], \xor , sub, shl, beqz);
  or or_2 (ALUop[1], sub, addi, add, lw, sw, bgt, beqz);
  or or_3 (ALUop[2], shra, shl, bgt, beqz);
  or or_4 (ALUop[3], jal, \output , \input , jr, j);
endmodule

module ALU (
  input  [15:0] rs_Data,
  input  [15:0] rt_Data,
  input  [3:0] ALUop,
  input  [2:0] shamt,
  output [15:0] Output_Data,
  output Output_Branch
);

  wire _0111_bgt_0110, _1000_beqz_0111;
  wire [15:0] _0000_nand_0000, _0001_xor_0001, _0100_sub_0011, _0101_shra_0100, _0110_shl_0101,
       addi_add_lw_sw_0010;

  assign _0000_nand_0000 = ~(rs_Data & rt_Data);  // NAND_Gate nand_1, 16 bits wide
  assign _0001_xor_0001 = rs_Data ^ rt_Data;  // XOR_Gate xor_1, 16 bits wide
  _16_bit_adder u_16_bit_adder_1 (
    .rs_Data(rs_Data), .rt_Data(rt_Data), .Sub(1'b0), .Output(addi_add_lw_sw_0010));  // open: ovf
  _16_bit_adder u_16_bit_adder_2 (
    .rs_Data(rs_Data), .rt_Data(rt_Data), .Sub(1'b1), .Output(_0100_sub_0011));  // open: ovf
  Right_Arith_Shift right_arith_shift_1 (.rs_Data(rs_Data), .shamt(shamt), .rs_Data_2(_0101_shra_0100));
  Left_Shift left_shift_1 (.rs_Data(rs_Data), .shamt(shamt), .rd_Data(_0110_shl_0101));
  BGT__rs____rt bgt_rs_rt_1 (.rs_Data(rs_Data), .rt_Data(rt_Data), .rs____rt(_0111_bgt_0110));
  BEQZ beqz_1 (.rs_Data(rs_Data), .beqz__rs(_1000_beqz_0111));
  Multiplexer #(.select(4), .width(16), .enable("false")) multiplexer_1 (
    .in0(_0000_nand_0000), .in1(_0001_xor_0001), .in2(addi_add_lw_sw_0010), .in3(_0100_sub_0011),
    .in4(_0101_shra_0100), .in5(_0110_shl_0101), .in6(rs_Data), .in7(rs_Data), .in8(rs_Data), .in9(rs_Data),
    .in10(rs_Data), .in11(rs_Data), .in12(rs_Data), .in13(rs_Data), .in14(rs_Data), .in15(rs_Data),
    .out(Output_Data), .sel(ALUop));
  Multiplexer #(.select(4), .enable("false")) multiplexer_2 (
    .in0(1'b0), .in1(1'b0), .in2(1'b0), .in3(1'b0), .in4(1'b0), .in5(1'b0), .in6(_0111_bgt_0110),
    .in7(_1000_beqz_0111), .in8(1'b0), .in9(1'b0), .in10(1'b0), .in11(1'b0), .in12(1'b0), .in13(1'b0),
    .in14(1'b0), .in15(1'b0), .out(Output_Branch), .sel(ALUop));

  // Other names for the same wires on the sheet: j_jr_jal_TTY_KB_1000[15:0] = rs_Data; rt_Immed_Data[15:0] = rt_Data
endmodule

module Instruction_Breakdown (
  input  [15:0] Instruction,
  output [3:0] opcode,
  output [2:0] Rs,
  output [2:0] Rt,
  output [2:0] Rd,
  output [2:0] shamt,
  output [5:0] Immediate,
  output [11:0] Address
);


  assign Address = Instruction[11:0];
  assign Immediate = Instruction[5:0];
  assign opcode = Instruction[15:12];
  assign Rd = Instruction[5:3];
  assign Rs = Instruction[11:9];
  assign Rt = Instruction[8:6];
  assign shamt = Instruction[2:0];

  // Other names for the same wires on the sheet: _0 = Instruction[0]; _1 = Instruction[1]; _2 = Instruction[2];
  //   _3 = Instruction[3]; _4 = Instruction[4]; _5 = Instruction[5]; _6 = Instruction[6]; _7 = Instruction[7];
  //   _8 = Instruction[8]; _9 = Instruction[9]; _10 = Instruction[10]; _11 = Instruction[11]; _12 = Instruction[12];
  //   _13 = Instruction[13]; _14 = Instruction[14]; _15 = Instruction[15]
endmodule

module PC___1 (
  output [15:0] PC_1
);


  assign PC_1 = 16'h1;
endmodule

module _128_binary (
  output [15:0] _128_binary
);


  assign _128_binary = 16'h80;
endmodule

module r7 (
  output [2:0] r7
);


  assign r7 = 3'b111;
endmodule

module PC (
  input  Reset,
  input  clk,
  input  writeEnable,
  input  [15:0] Input,
  output [15:0] Output
);

  D_Flip_Flop d_ff_1 (.clk(clk), .D(Input[0]), .Q(Output[0]), .en(writeEnable), .reset(Reset));  // open: Qn, preset
  D_Flip_Flop d_ff_2 (.clk(clk), .D(Input[1]), .Q(Output[1]), .en(writeEnable), .reset(Reset));  // open: Qn, preset
  D_Flip_Flop d_ff_3 (.clk(clk), .D(Input[2]), .Q(Output[2]), .en(writeEnable), .reset(Reset));  // open: Qn, preset
  D_Flip_Flop d_ff_4 (.clk(clk), .D(Input[3]), .Q(Output[3]), .en(writeEnable), .reset(Reset));  // open: Qn, preset
  D_Flip_Flop d_ff_5 (.clk(clk), .D(Input[4]), .Q(Output[4]), .en(writeEnable), .reset(Reset));  // open: Qn, preset
  D_Flip_Flop d_ff_6 (.clk(clk), .D(Input[5]), .Q(Output[5]), .en(writeEnable), .reset(Reset));  // open: Qn, preset
  D_Flip_Flop d_ff_7 (.clk(clk), .D(Input[6]), .Q(Output[6]), .en(writeEnable), .reset(Reset));  // open: Qn, preset
  D_Flip_Flop d_ff_8 (.clk(clk), .D(Input[7]), .Q(Output[7]), .en(writeEnable), .reset(Reset));  // open: Qn, preset
  D_Flip_Flop d_ff_9 (.clk(clk), .D(Input[8]), .Q(Output[8]), .en(writeEnable), .reset(Reset));  // open: Qn, preset
  D_Flip_Flop d_ff_10 (.clk(clk), .D(Input[9]), .Q(Output[9]), .en(writeEnable), .reset(Reset));  // open: Qn, preset
  D_Flip_Flop d_ff_11 (.clk(clk), .D(Input[10]), .Q(Output[10]), .en(writeEnable), .reset(Reset));  // open: Qn, preset
  D_Flip_Flop d_ff_12 (.clk(clk), .D(Input[11]), .Q(Output[11]), .en(writeEnable), .reset(Reset));  // open: Qn, preset
  D_Flip_Flop d_ff_13 (.clk(clk), .D(Input[12]), .Q(Output[12]), .en(writeEnable), .reset(Reset));  // open: Qn, preset
  D_Flip_Flop d_ff_14 (.clk(clk), .D(Input[13]), .Q(Output[13]), .en(writeEnable), .reset(Reset));  // open: Qn, preset
  D_Flip_Flop d_ff_15 (.clk(clk), .D(Input[14]), .Q(Output[14]), .en(writeEnable), .reset(Reset));  // open: Qn, preset
  D_Flip_Flop d_ff_16 (.clk(clk), .D(Input[15]), .Q(Output[15]), .en(writeEnable), .reset(Reset));  // open: Qn, preset
endmodule

module _6_bit_Sign_Ext (
  input  [5:0] _6_bit_Immed,
  output [15:0] _16_bit_Immed
);


  assign _16_bit_Immed = {{11{_6_bit_Immed[5]}}, _6_bit_Immed[4:0]};
endmodule

module _7_bit_Zero_Extender (
  input  [6:0] _7_bit_ASCII_Value,
  output [15:0] _16_bit_ASCII_value
);


  assign _16_bit_ASCII_value = {{9{1'b0}}, _7_bit_ASCII_Value};
endmodule
